# Fritzing sketch Schaltplan (saved by Fritzing 0.9.4)

parts:
  S1_HOCH = Pushbutton [package=THT]
  S6_VORWAERTS = Pushbutton [package=THT]
  S5_ZURUECK = Pushbutton [package=THT]
  S4_RECHTS = Pushbutton [package=THT]
  S2_RUNTER = Pushbutton [package=THT]
  S3_LINKS = Pushbutton [package=THT]
  part = Raspberry Pi 3 [part_number=RPI-3-V1.2]
  4_Channel_Relay1 = 4 Channel Power Relay
  4_Channel_Relay2 = 4 Channel Power Relay

nets:
  GND: S1_HOCH.leg0, S6_VORWAERTS.leg0, S5_ZURUECK.leg0, S4_RECHTS.leg0, S2_RUNTER.leg0, S3_LINKS.leg0, part.GND, 4_Channel_Relay1.GND, 4_Channel_Relay2.GND
  N1: S1_HOCH.leg1, part.GIPO26
  N2: S6_VORWAERTS.leg1, part.GPIO2
  N3: S5_ZURUECK.leg1, part.GIPO21
  N4: S4_RECHTS.leg1, part.GIPO4
  N5: S2_RUNTER.leg1, part.GIPO19
  N6: S3_LINKS.leg1, part.GPIO3
  VCC: part.5V, 4_Channel_Relay1.VCC, 4_Channel_Relay2.VCC

custom parts:
  4 Channel Power Relay: A 4 channel power relay. The module operates at 5V.
